# Fritzing sketch SensorBoard (saved by Fritzing 0.9.2b)
circuit board: 3.0736cm x 3.11901cm
circuit board: 6.03156cm x 3.14732cm
breadboards: 2

parts:
  R2 = Resistor [tolerance=±5% resistance=22k package=THT]
  FR = Photocell (LDR) [package=THT]
  NTC = Temperature Sensor (Thermistor) [thermistor_type=NTC package=THT]
  J2 = female pin header, 2 pins [form="♀ (female)"]
  R4 = Resistor [tolerance=±5% resistance=2.2k package=THT]
  R3 = Resistor [tolerance=±5% resistance=2.2k package=THT]
  R1 = Resistor [tolerance=±0.25% resistance=15k package=THT]
  J5 = female pin header, 4 pins [form="♀ (female)"]
  Componente1 = Arduino Nano (Rev3.0) (ICSP)
  J6 = female pin header, 6 pins [form="♀ (female)"]
  J7 = female pin header, 6 pins [form="♀ (female)"]
  LED1 = LED - 3mm [color="Red (635nm)" package="3 mm [THT]"]

nets:
  N1: R2.Pin_0, R4.Pin_0, R3.Pin_0, R1.Pin_0, J5.pin1, Componente1.D6, J6.pin2, J7.pin2
  N2: R2.Pin_1, FR.pin_1, Componente1.A4, J7.pin4
  N3: FR.pin_0, NTC.pin_0, J2.pin1, J5.pin2, Componente1.GND, J6.pin1, J7.pin1, LED1.cathode
  N4: NTC.pin_1, R1.Pin_1, Componente1.A5, J6.pin3, J7.pin3
  N5: J2.pin2, R3.Pin_1, Componente1.D5, J6.pin6, J7.pin6
  N6: R4.Pin_1, LED1.anode
  N7: J5.pin4, Componente1.A3, J6.pin5, J7.pin5

notes:
  soil sensor
  pump
  arduino
  components on breadboard side
